# Fritzing sketch Spear (saved by Fritzing 0.9.3b)
breadboards: 1

parts:
  Componente1 = Arduino Mega 2560 (Rev3)
  R1 = Photocell (LDR) [package=THT]  # not connected
  S1 = Pushbutton [package="[THT]"]  # not connected
  S2 = Pushbutton [package="[THT]"]  # not connected
  S3 = Pushbutton [package="[THT]"]  # not connected
  S4 = Pushbutton [package="[THT]"]  # not connected
  S6 = Pushbutton [package="[THT]"]  # not connected
  LCD1 = LCD screen
  R2 = Rotary Potentiometer (Small) [maximum_resistance=100kΩ package=THT]
  Componente2 = Adafruit Motor/Stepper/Servo Shield [part_number="Adafruit #1438"]
  KEYPAD1 = Membrane Matrix Keypad
  Componente5 = Adafruit TSL2591 [part_number="Adafruit #1980"]
  IR1 = TSOP312.., 314.. [package=THT]  # not connected
  Componente6 = Adafruit DS1307 RTC Breakout [part_number="Adafruit #264"]
  M1 = Stepper Motor - Bipolar
  JACK1 = 2.1mm Barrel Jack with Terminal Block

nets:
  N1: Componente1.D21/SCL, Componente2.AD5/SCL, Componente5.SCL, Componente6.SCL
  N2: Componente1.D20/SDA, Componente2.AD4/SDA, Componente5.SDA, Componente6.SDA
  GND: Componente1.GND, LCD1.VSS, LCD1.R/W, LCD1.LED-, R2.leg1, Componente5.GND, Componente6.GND
  VIN: Componente1.VIN, LCD1.VDD, LCD1.LED+, R2.leg2, Componente5.VIN, Componente6.VCC
  N3: Componente1.D32, KEYPAD1.7
  N4: Componente1.D33, KEYPAD1.6
  N5: Componente1.D34, KEYPAD1.5
  N6: Componente1.D35, KEYPAD1.4
  N7: Componente1.D36, KEYPAD1.3
  N8: Componente1.D37, KEYPAD1.2
  N9: Componente1.D38, KEYPAD1.1
  N10: LCD1.V0, R2.wiper
  N11: Componente2.M3A, M1.D
  N12: Componente2.M3B, M1.B
  N13: Componente2.M4B, M1.C
  N14: Componente2.M4A, M1.A
  N15: Componente2.GND, JACK1.POS
  N16: Componente2.VMOTOR, JACK1.NEG

custom parts:
  Adafruit Motor/Stepper/Servo Shield: The original Adafruit Motorshield kit is one of our most beloved kits, which is why we decided to make something even better. We have upgraded the shield kit to make the bestest, easiest way to drive DC and Stepper motors. This shield will make quick work of your next robotics project! We kept the ability to drive up to 4 DC motors or 2 stepper motors, but added many improvements: Instead of a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
  Membrane Matrix Keypad: Membrane Matrix 3x4 Keypad
  Adafruit TSL2591: When the future is dazzlingly-bright, this ultra-high-range luminosity sensor will help you measure it. The TSL2591 luminosity sensor is an advanced digital light sensor, ideal for use in a wide range of light situations. Compared to low cost CdS cells, this sensor is more precise, allowing for exact lux calculations and can be configured for different gain/timing ranges to detect light ranges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
  Adafruit DS1307 RTC Breakout: This is a great battery-backed real time clock (RTC) that allows your microcontroller project to keep track of time even if it is reprogrammed, or if the power is lost. Perfect for datalogging, clock-building, time stamping, timers and alarms, etc. The DS1307 is the most popular RTC - but it requires 5V power to work (although we've used it with 5V power and 3.3V logic successfully) PCB &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
